// Digital circuit a-risc.dig as structural Verilog
module a_risc (
  input  C,
  input  V,
  input  G,
  input  R,
  output W,
  output [7:0] D,
  output [15:0] A
);

  wire ADD, ALU, AND, AWe_R, AWe_R0, B, Branch, C_A_plus_B, Cond, CR, cy, EOR, EXEC_WeR, EXECUTE, FETCH_IR1,
       FETCH_IR2, FETCHING, LHH, LHI, LHL, LLH, LLI, LLL, LSXX, LWH, LWL, N, od, ORR, ov, S_Da___eq_S_Db,
       S_Da__eq_S_Db, SUB, SWH, SWL, UsePR, V_Q_t, We_R;
  wire [1:0] S;
  wire [3:0] Ra_t, Rb_t, Rc_t;
  wire [4:0] FR;
  wire [7:0] AH, im8, IR1, psw;
  wire [14:1] Q_t_t;
  wire [15:0] A_B, A_B_t, A_plus_B, AB, AH_lt__eq___B_plus_i4, ARMAR, branchBy, nDb, NewPR, plus_B, Q_t,
       Q_t_t_t, RMAR, sexi4, sexim8, sexim8_3;
  wire [15:8] AH_lt__eq_BH, AH_lt__eq_BL;

  PowerSupply powersupply_1 (.VDD(V), .GND(G));
  Decoder #(.Selector_Bits(2)) decoder_1 (
    .sel(S), .out_0(FETCH_IR1), .out_1(FETCH_IR2), .out_2(EXECUTE));  // open: out_3
  Demultiplexer #(.Selector_Bits(4)) demultiplexer_1 (
    .sel(IR1[3:0]), .in(EXECUTE), .out_0(ADD), .out_1(SUB), .out_2(EOR), .out_3(ORR), .out_4(AND),
    .out_5(LLI), .out_6(LHI), .out_7(B), .out_8(LWL), .out_9(SWL), .out_10(LWH), .out_11(SWH), .out_12(LLL),
    .out_13(LLH), .out_14(LHL), .out_15(LHH));
  Counter #(.Bits(2)) counter_1 (.en(1'b1), .C(C), .clr(N), .out(S));  // open: ovf
  Register #(.Bits(8)) IR2 (.D(AH_lt__eq___B_plus_i4[15:8]), .C(C), .en(FETCH_IR2), .Q(im8));
  Register #(.Bits(8)) u_IR1 (.D(AH_lt__eq___B_plus_i4[15:8]), .C(C), .en(FETCH_IR1), .Q(IR1));
  RegisterFile #(.AddrBits(4), .Bits(16)) RF (
    .Din(Q_t), .we(We_R), .Rw(Ra_t), .C(C), .Ra(Rb_t), .Rb(Rc_t), .Da({AH, AH_lt__eq___B_plus_i4[7:0]}),
    .Db({AH_lt__eq_BH, AH_lt__eq_BL}));
  Register #(.Bits(8)) u_PSW (
    .D({3'b000, FR[4:3], C_A_plus_B, FR[1:0]}), .C(C), .en(ALU), .Q({psw[7:5], od, psw[3], cy, ov, psw[0]}));
  Add #(.Bits(16)) add_1 (.a(sexim8), .b(16'hfffd), .c_i(1'b0), .s(sexim8_3));  // open: c_o
  Add #(.Bits(16)) add_2 (.a({AH, AH_lt__eq___B_plus_i4[7:0]}), .b(branchBy), .c_i(1'b1), .s(NewPR));  // open: c_o
  Add #(.Bits(16)) add_3 (.a(RMAR), .b(sexi4), .c_i(1'b0), .s(ARMAR));  // open: c_o
  BitExtender #(.inputBits(4)) bitextender_1 (.in(im8[7:4]), .out(sexi4));
  BitExtender bitextender_2 (.in(im8), .out(sexim8));
  Multiplexer #(.Bits(4)) multiplexer_1 (.sel(UsePR), .in_0(IR1[7:4]), .in_1(4'b0000), .out(Ra_t));
  Multiplexer #(.Bits(4)) multiplexer_2 (.sel(UsePR), .in_0(im8[3:0]), .in_1(4'b0000), .out(Rb_t));
  Multiplexer #(.Bits(4)) multiplexer_3 (.sel(LSXX), .in_0(im8[7:4]), .in_1(Ra_t), .out(Rc_t));
  Multiplexer #(.Bits(16)) multiplexer_4 (.sel(SUB), .in_0({AH_lt__eq_BH, AH_lt__eq_BL}), .in_1(nDb), .out(plus_B));
  Multiplexer #(.Bits(16)) multiplexer_5 (
    .sel(W), .in_0({AH, AH_lt__eq___B_plus_i4[7:0]}), .in_1({AH_lt__eq_BH, AH_lt__eq_BL}), .out(RMAR));
  Multiplexer #(.Bits(16)) multiplexer_6 (.sel(B), .in_0({16{1'b0}}), .in_1(sexim8_3), .out(branchBy));
  Multiplexer #(.Bits(16)) multiplexer_7 (.sel(UsePR), .in_0({FR[3], Q_t_t, FR[4]}), .in_1(NewPR), .out(Q_t_t_t));
  Multiplexer #(.Bits(16)) multiplexer_8 (
    .sel(EXECUTE), .in_0({AH, AH_lt__eq___B_plus_i4[7:0]}), .in_1(ARMAR), .out(A));
  assign Q_t = ~R ? Q_t_t_t : 16'bz;  // DriverInvSel driverinvsel_1
  or or_1 (N, R, EXECUTE);
  PullDown #(.Bits(16)) pulldown_1 (.out(Q_t));
  assign nDb = ~{AH_lt__eq_BH, AH_lt__eq_BL};  // Not not_1, 16 bits wide
  Add #(.Bits(16)) add_4 (.a({AH, AH_lt__eq___B_plus_i4[7:0]}), .b(plus_B), .c_i(CR), .s(A_plus_B), .c_o(C_A_plus_B));
  assign A_B = {AH, AH_lt__eq___B_plus_i4[7:0]} ^ {AH_lt__eq_BH, AH_lt__eq_BL};  // XOr xor_1, 16 bits wide
  assign A_B_t = {AH, AH_lt__eq___B_plus_i4[7:0]} | {AH_lt__eq_BH, AH_lt__eq_BL};  // Or or_2, 16 bits wide
  assign AB = {AH, AH_lt__eq___B_plus_i4[7:0]} & {AH_lt__eq_BH, AH_lt__eq_BL};  // And and_1, 16 bits wide
  xor xor_2 (CR, SUB, cy);
  or or_3 (AWe_R0, LHI, LLI, LHH, LHL, ALU, LLH, LLL, LWH, LWL);
  or or_4 (AWe_R, AWe_R0, Branch);
  or or_5 (W, SWH, SWL);
  or or_6 (UsePR, FETCHING, B);
  and and_2 (Branch, B, Cond);
  and and_3 (EXEC_WeR, EXECUTE, AWe_R);
  or or_7 (FETCHING, FETCH_IR2, FETCH_IR1);
  or or_8 (We_R, EXEC_WeR, FETCH_IR2, FETCH_IR1);
  or or_9 (LSXX, W, SWL, LWL);
  or or_10 (ALU, AND, ORR, EOR, SUB, ADD);
  xor xor_3 (S_Da__eq_S_Db, AH[7], AH_lt__eq_BH[15]);
  xor xor_4 (S_Da___eq_S_Db, S_Da__eq_S_Db, SUB);
  xnor xnor_1 (V_Q_t, AH[7], FR[3]);
  and and_4 (FR[1], S_Da___eq_S_Db, V_Q_t);
  Comparator #(.Bits(16)) comparator_1 (.a({FR[3], Q_t_t, FR[4]}), .b({16{1'b0}}), .eq(FR[0]));  // open: gt, lt
  Multiplexer #(.Selector_Bits(4), .Bits(16)) multiplexer_9 (
    .sel(IR1[3:0]), .in_0(A_plus_B), .in_1(A_plus_B), .in_2(A_B), .in_3(A_B_t), .in_4(AB),
    .in_5({{8{1'b0}}, im8}), .in_6({im8, {8{1'b0}}}), .in_7({16{1'b0}}),
    .in_8({AH, AH_lt__eq___B_plus_i4[15:8]}), .in_9({{8{1'b0}}, AH_lt__eq___B_plus_i4[7:0]}),
    .in_10(AH_lt__eq___B_plus_i4), .in_11({{8{1'b0}}, AH}), .in_12({AH, AH_lt__eq_BL}),
    .in_13({AH, AH_lt__eq_BH}), .in_14({AH_lt__eq_BL, AH_lt__eq___B_plus_i4[7:0]}),
    .in_15({AH_lt__eq_BH, AH_lt__eq___B_plus_i4[7:0]}), .out({FR[3], Q_t_t, FR[4]}));
  Multiplexer #(.Selector_Bits(4)) multiplexer_10 (
    .sel(IR1[7:4]), .in_0(psw[0]), .in_1(ov), .in_2(cy), .in_3(psw[3]), .in_4(od), .in_5(1'b1), .in_6(1'b0),
    .in_7(1'b0), .in_8(1'b0), .in_9(1'b0), .in_10(1'b0), .in_11(1'b0), .in_12(1'b0), .in_13(1'b0),
    .in_14(1'b0), .in_15(1'b0), .out(Cond));
  // PinControl #(.Bits(8)) pincontrol_1: pin names not known; wires that end beside it: Q_t[7:0], W, AH_lt__eq___B_plus_i4[15:8], D

  // Other names for the same wires on the sheet: FR[2] = C_A_plus_B; AH_lt__eq_BH[7:0] = AH_lt__eq___B_plus_i4[7:0];
  //   AH_lt__eq_BL[7:0] = AH_lt__eq___B_plus_i4[7:0]; AL[7:0] = AH_lt__eq___B_plus_i4[7:0];
  //   Da[15:0] = {AH, AH_lt__eq___B_plus_i4[7:0]}; EXAL[7:0] = AH_lt__eq___B_plus_i4[7:0];
  //   O_Da = AH_lt__eq___B_plus_i4[0]; AL_lt__eq___B_plus_i4[15:0] = {AH, AH_lt__eq___B_plus_i4[15:8]};
  //   AL_lt__eq_BH[15:0] = {AH, AH_lt__eq_BH}; AL_lt__eq_BL[15:0] = {AH, AH_lt__eq_BL}; EXAH[7:0] = AH; S_Da = AH[7];
  //   BL[7:0] = AH_lt__eq_BL; Db[15:0] = {AH_lt__eq_BH, AH_lt__eq_BL}; O_Db = AH_lt__eq_BL[8]; BH[7:0] = AH_lt__eq_BH;
  //   S_Db = AH_lt__eq_BH[15]; Di[7:0] = AH_lt__eq___B_plus_i4[15:8]; im8_as_H[15:8] = im8; im8_as_L[7:0] = im8;
  //   IR2[7:0] = im8; Rb[3:0] = im8[3:0]; Rc[3:0] = im8[7:4]; OP[3:0] = IR1[3:0]; Ra[3:0] = IR1[7:4]; MAR[15:0] = A;
  //   ze = psw[0]; psw (some bits) = {od, cy, ov}; sg = psw[3]; Q = FR[0]; QL[7:0] = Q_t[7:0]; QH[7:0] = Q_t[15:8];
  //   O_Q = FR[4]; Q_t_t (some bits) = {FR[3], FR[4]}; S_Q = FR[3]; RMAR_DIR = W; V_Q = FR[1]

  // Notes on the sheet:
  //   C: Hz: 16
  //   W: Write instead of Read
  //   V: default 1
  //   R: Reset, default 1
  //   CPU
endmodule
