// Digital circuit design.dig as structural Verilog
module \design  (
  input  clk
);

  wire LD, LD_t, not_1_out, not_2_out, R_W, ST, ST_t;
  wire [7:0] D;
  wire [15:0] A;

  GraphicCard #(.graphicHeight(128), .Bits(8), .graphicWidth(128)) graphiccard_1 (
    .A(A[14:0]), .str(ST_t), .C(clk), .ld(LD_t), .B(1'b0), .D(D));
  EEPROMDualPort #(.AddrBits(15), .Bits(8)) eepromdualport_1 (.A(A[14:0]), .Din(D), .str(ST), .C(clk), .ld(LD), .D(D));
  a_risc a_risc_1 (.C(clk), .V(1'b1), .G(1'b0), .R(1'b0), .R_W(R_W), .D(D), .A(A));
  not not_1 (not_1_out, R_W);
  not not_2 (not_2_out, R_W);
  and and_1 (LD_t, not_1_out, A[15]);
  and and_2 (LD, not_2_out, ~A[15]);  // And
  and and_3 (ST_t, R_W, A[15]);
  and and_4 (ST, R_W, ~A[15]);  // And

  // Other names for the same wires on the sheet: A_t[14:0] = A[14:0]; B = A[15]; C = clk

  // Notes on the sheet:
  //   clk: Hz: 16
  //   contents of eepromdualport_1 (hex, n*v repeats v):
  //   15,6,25,9,30,12,58,1e,e9,15,57,fffffffffffffff6
endmodule
